// Digital circuit lc3-SPRAM_HDL.dig as structural Verilog
module lc3_SPRAM_HDL (
  input  [15:0] ADDRESS,
  input  [15:0] DATAIN,
  input  WREN,
  input  CLOCK,
  output [15:0] DATAOUT,
  output R
);

  wire comparator_1_eq, comparator_1_gt, decoder_1_out_0, decoder_1_out_1, decoder_1_out_2, decoder_1_out_3,
       not_1_out;
  wire [1:0] counter_1_out;
  wire [3:3] and_1_out, and_2_out, and_3_out, and_4_out;
  wire [15:0] u_SB_SPRAM256KA_2_dataout, u_SB_SPRAM256KA_3_dataout, u_SB_SPRAM256KA_4_dataout,
       u_SB_SPRAM256KA_dataout;

  Decoder #(.Selector_Bits(2)) decoder_1 (
    .sel(ADDRESS[15:14]), .out_0(decoder_1_out_0), .out_1(decoder_1_out_1), .out_2(decoder_1_out_2),
    .out_3(decoder_1_out_3));
  and and_1 (and_1_out[3], decoder_1_out_0, WREN);
  and and_2 (and_2_out[3], decoder_1_out_1, WREN);
  and and_3 (and_3_out[3], decoder_1_out_2, WREN);
  and and_4 (and_4_out[3], decoder_1_out_3, WREN);
  SB_SPRAM256KA #(.applicationType("IVERILOG"), .CodeFile("/home/allan/cs061/LC3_realized/ice_ip.v")) u_SB_SPRAM256KA (
    .ADDRESS(ADDRESS[13:0]), .DATAIN(DATAIN), .MASKWREN({4{and_1_out[3]}}), .WREN(and_1_out[3]),
    .CHIPSELECT(1'b1), .CLOCK(CLOCK), .STANDBY(1'b0), .SLEEP(1'b0), .POWEROFF(1'b1),
    .DATAOUT(u_SB_SPRAM256KA_dataout));
  SB_SPRAM256KA #(.applicationType("IVERILOG"), .CodeFile("/home/allan/cs061/LC3_realized/ice_ip.v")) u_SB_SPRAM256KA_2 (
    .ADDRESS(ADDRESS[13:0]), .DATAIN(DATAIN), .MASKWREN({4{and_2_out[3]}}), .WREN(and_2_out[3]),
    .CHIPSELECT(1'b1), .CLOCK(CLOCK), .STANDBY(1'b0), .SLEEP(1'b0), .POWEROFF(1'b1),
    .DATAOUT(u_SB_SPRAM256KA_2_dataout));
  SB_SPRAM256KA #(.applicationType("IVERILOG"), .CodeFile("/home/allan/cs061/LC3_realized/ice_ip.v")) u_SB_SPRAM256KA_3 (
    .ADDRESS(ADDRESS[13:0]), .DATAIN(DATAIN), .MASKWREN({4{and_3_out[3]}}), .WREN(and_3_out[3]),
    .CHIPSELECT(1'b1), .CLOCK(CLOCK), .STANDBY(1'b0), .SLEEP(1'b0), .POWEROFF(1'b1),
    .DATAOUT(u_SB_SPRAM256KA_3_dataout));
  SB_SPRAM256KA #(.applicationType("IVERILOG"), .CodeFile("/home/allan/cs061/LC3_realized/ice_ip.v")) u_SB_SPRAM256KA_4 (
    .ADDRESS(ADDRESS[13:0]), .DATAIN(DATAIN), .MASKWREN({4{and_4_out[3]}}), .WREN(and_4_out[3]),
    .CHIPSELECT(1'b1), .CLOCK(CLOCK), .STANDBY(1'b0), .SLEEP(1'b0), .POWEROFF(1'b1),
    .DATAOUT(u_SB_SPRAM256KA_4_dataout));
  Counter #(.Bits(2)) counter_1 (.en(not_1_out), .C(CLOCK), .clr(WREN), .out(counter_1_out));  // open: ovf
  not not_1 (not_1_out, WREN);
  Comparator #(.Bits(2)) comparator_1 (
    .a(counter_1_out), .b(2'b11), .gt(comparator_1_gt), .eq(comparator_1_eq));  // open: lt
  or or_1 (R, WREN, comparator_1_gt, comparator_1_eq);
  Multiplexer #(.Selector_Bits(2), .Bits(16)) multiplexer_1 (
    .sel(ADDRESS[15:14]), .in_0(u_SB_SPRAM256KA_dataout), .in_1(u_SB_SPRAM256KA_2_dataout),
    .in_2(u_SB_SPRAM256KA_3_dataout), .in_3(u_SB_SPRAM256KA_4_dataout), .out(DATAOUT));

  // Other names for the same wires on the sheet: C = CLOCK; clr = WREN
endmodule
