// Digital circuit lc3-acv.dig as structural Verilog
module lc3_acv (
  input  mode,
  input  [6:0] in,
  input  clk,
  input  en,
  output ACV
);

  wire and_1_out, and_2_out, and_3_out, and_4_out, or_1_out, or_2_out;

  and and_1 (and_1_out, ~in[6], ~in[5]);  // And
  or or_1 (or_1_out, ~in[4], ~in[3]);  // Or
  and and_2 (and_2_out, in[6], in[5], in[4], in[3], in[2], in[1], in[0]);
  and and_3 (and_3_out, and_1_out, or_1_out);
  or or_2 (or_2_out, and_3_out, and_2_out);
  and and_4 (and_4_out, mode, or_2_out);
  Register register_1 (.D(and_4_out), .C(clk), .en(en), .Q(ACV));
endmodule
