// Digital circuit lc3-alu.dig as structural Verilog
module lc3_alu (
  input  [15:0] A,
  input  [15:0] B,
  input  [1:0] ALUK,
  output [15:0] ALU
);

  wire [15:0] ADD_s, and_1_out, not_1_out;

  Add #(.Bits(16)) ADD (.a(A), .b(B), .c_i(1'b0), .s(ADD_s));  // open: c_o
  assign and_1_out = A & B;  // And and_1, 16 bits wide
  assign not_1_out = ~A;  // Not not_1, 16 bits wide
  Multiplexer #(.Selector_Bits(2), .Bits(16)) multiplexer_1 (
    .sel(ALUK), .in_0(ADD_s), .in_1(and_1_out), .in_2(not_1_out), .in_3(A), .out(ALU));
endmodule
