// Digital circuit lc3-breakpoint.dig as structural Verilog
module lc3_breakpoint (
  input  [15:0] Breakpoint,
  input  [15:0] PC,
  input  [5:0] State,
  input  en
);

  wire and_1_out, comparator_1_eq, comparator_2_eq;

  Comparator #(.Bits(16)) comparator_1 (.a(Breakpoint), .b(PC), .eq(comparator_1_eq));  // open: gt, lt
  Comparator #(.Bits(6)) comparator_2 (.a(State), .b(6'b010010), .eq(comparator_2_eq));  // open: gt, lt
  and and_1 (and_1_out, en, comparator_1_eq, comparator_2_eq);
  Break #(.Cycles(1000000)) break_1 (.brk(and_1_out));
  // Pins of 1 and 16 bits meet at PC
  // Pins of 1 and 6 bits meet at State

  // Notes on the sheet:
  //   Breakpoint: default 65535
endmodule
