// Digital circuit lc3-cc-logic.dig as structural Verilog
module lc3_cc_logic (
  input  [15:0] D_in,
  output N,
  output Z,
  output P
);

  Comparator #(.Bits(16)) comparator_1 (.a(D_in), .b({16{1'b0}}), .eq(Z));  // open: gt, lt
  and and_1 (P, ~Z, ~D_in[15]);  // And

  assign N = D_in[15];
endmodule
