// Digital circuit lc3-control.dig as structural Verilog
module lc3_control (
  input  Clk,
  input  INT,
  input  R,
  input  [4:0] IR_15_11,
  input  BEN,
  input  PSR_15,
  input  ACV,
  output LD_MAR,
  output LD_MDR,
  output LD_IR,
  output LD_BEN,
  output LD_REG,
  output LD_CC,
  output LD_PC,
  output LD_Priv,
  output LD_SavedSSP,
  output LD_SavedUSP,
  output LD_Vector,
  output LD_ACV,
  output GatePC,
  output GateMDR,
  output GateALU,
  output GateMARMUX,
  output GateVector,
  output GatePC_1,
  output GatePSR,
  output GateSP,
  output [1:0] PCMUX,
  output [1:0] DRMUX,
  output [1:0] SR1MUX,
  output [1:0] ADDR2MUX,
  output [1:0] SPMUX,
  output [1:0] ALUK,
  output ADDR1MUX,
  output MARMUX,
  output TableMUX,
  output PSRMUX,
  output MIO_EN,
  output R_W,
  output Set_Priv,
  output [5:0] State
);

  wire [9:0] J_Cond_IRD, register_1_q, register_2_q;
  wire [30:6] LC3_Microcode_d;

  Register #(.Bits(10)) register_1 (.D(J_Cond_IRD), .C(Clk), .en(Clk), .Q(register_1_q));
  Register #(.Bits(10)) register_2 (.D({ACV, PSR_15, BEN, IR_15_11, R, INT}), .C(Clk), .en(Clk), .Q(register_2_q));
  lc3_microsequencer lc3_microsequencer_1 (
    .J(register_1_q[5:0]), .COND(register_1_q[8:6]), .IRD(register_1_q[9]), .INT(register_2_q[0]),
    .R(register_2_q[1]), .IR_15_11(register_2_q[6:2]), .BEN(register_2_q[7]), .PSR_15(register_2_q[8]),
    .ACV(register_2_q[9]), .Addr(State));
  ROM #(.AddrBits(6), .Bits(52)) LC3_Microcode (
    .A(State), .sel(1'b1),
    .D({J_Cond_IRD, LD_MAR, LD_MDR, LD_IR, LD_BEN, LD_REG, LD_CC, LD_PC, LD_Priv, LD_SavedSSP, LD_SavedUSP, LD_Vector, LC3_Microcode_d[30], LD_ACV, GatePC, GateMDR, GateALU, GateMARMUX, GateVector, GatePC_1, GatePSR, GateSP, PCMUX, DRMUX, SR1MUX, ADDR1MUX, ADDR2MUX, SPMUX, MARMUX, TableMUX, LC3_Microcode_d[7:6], PSRMUX, ALUK, MIO_EN, R_W, Set_Priv}));

  // Notes on the sheet:
  //   contents of LC3_Microcode (hex, n*v repeats v):
  //   2480000000000,483004008000,8e0022002200,5e0022002200,3500000000000
  //   ,483004008008,8e002200d200,5e002200d200,4920004010018,483004008010
  //   ,460022002200,4e0022002200,480804088018,4950480400180,482002002200
  //   ,bd0880400000,1400000000006,6600000000000,860830000000,6740000000000
  //   ,48281012c000,482810123000,480802082200,6410004000018,1610000000004
  //   ,1650000000004,8e0028000000,483008000000,1710000000004,1750000000004
  //   ,808008000000,5e0028000000,8004000000000,6700000000000,4cc2000250000
  //   ,6640000000000,1910000000004,a62000250400,9c0808080000,a22000250000
  //   ,1a10000000004,1a40000000006,881448000020,b90000800000,b50480400140
  //   ,942100250800,d22000250400,4940482000000,d504804001c0,4950480400100
  //   ,0,480000000000,1d00000000006,1d50000000004,d60001000000,480808080000
  //   ,b504804001c0,b504804001c0,0,482200250c00,b504804001c0,b504804001c0
endmodule
