// Digital circuit lc3-details.dig as structural Verilog
module lc3_details (
  input  Clk,
  input  LD_SavedSSP,
  input  LD_SavedUSP,
  input  GateSP,
  input  [1:0] SPMUX,
  input  [15:0] SR1_Val,
  input  TableMux,
  input  LD_Vector,
  input  GateVector,
  input  N,
  input  Z,
  input  P,
  input  [2:0] IR_2_0,
  input  LD_BEN,
  input  LD_ACV,
  input  Set_Priv,
  input  PSRMux,
  input  GatePSR,
  input  LD_Priv,
  input  [15:0] Bus,
  output [15:0] GatedSP,
  output [15:0] GatedVector,
  output [15:0] GatedPSR,
  output BEN,
  output ACV,
  output PSR_15
);

  wire and_1_out, and_2_out, and_3_out, multiplexer_1_out, or_1_out;
  wire [7:0] multiplexer_2_out, Vector_q;
  wire [15:0] add_1_s, multiplexer_3_out, Saved_SSP_q, Saved_USP_q, sub_1_s;

  Multiplexer multiplexer_1 (.sel(PSRMux), .in_0(Set_Priv), .in_1(Bus[15]), .out(multiplexer_1_out));
  Multiplexer #(.Bits(8)) multiplexer_2 (.sel(TableMux), .in_0(Bus[7:0]), .in_1({8{1'b0}}), .out(multiplexer_2_out));
  Register Priv (.D(multiplexer_1_out), .C(Clk), .en(LD_Priv), .Q(PSR_15));
  Register #(.Bits(16)) Saved_SSP (.D(SR1_Val), .C(Clk), .en(LD_SavedSSP), .Q(Saved_SSP_q));
  Register #(.Bits(16)) Saved_USP (.D(SR1_Val), .C(Clk), .en(LD_SavedUSP), .Q(Saved_USP_q));
  and and_1 (and_1_out, N, IR_2_0[2]);
  and and_2 (and_2_out, Z, IR_2_0[1]);
  and and_3 (and_3_out, P, IR_2_0[0]);
  Add #(.Bits(16)) add_1 (.a(SR1_Val), .b(16'h1), .c_i(1'b0), .s(add_1_s));  // open: c_o
  Sub #(.Bits(16)) sub_1 (.a(SR1_Val), .b(16'h1), .c_i(1'b0), .s(sub_1_s));  // open: c_o
  Register #(.Bits(8)) Vector (.D(multiplexer_2_out), .C(Clk), .en(LD_Vector), .Q(Vector_q));
  lc3_acv lc3_acv_1 (.mode(PSR_15), .in(Bus[15:9]), .clk(Clk), .en(LD_ACV), .ACV(ACV));
  or or_1 (or_1_out, and_1_out, and_2_out, and_3_out);
  assign GatedPSR = GatePSR ? {PSR_15, {12{1'b0}}, N, Z, P} : 16'bz;  // Driver driver_1
  Multiplexer #(.Selector_Bits(2), .Bits(16)) multiplexer_3 (
    .sel(SPMUX), .in_0(add_1_s), .in_1(sub_1_s), .in_2(Saved_SSP_q), .in_3(Saved_USP_q),
    .out(multiplexer_3_out));
  assign GatedVector = GateVector ? {{8{1'b0}}, Vector_q} : 16'bz;  // Driver driver_2
  Register u_BEN (.D(or_1_out), .C(Clk), .en(LD_BEN), .Q(BEN));
  assign GatedSP = GateSP ? multiplexer_3_out : 16'bz;  // Driver driver_3

  // Notes on the sheet:
  //   Processor Status Register
  //   Access Control Violation
  //   Branch Enable
  //   Stack Pointer
  //   Vector'Table
endmodule
