// Digital circuit lc3-halt.dig as structural Verilog
module lc3_halt (
  input  [15:0] MAR,
  input  [15:0] D_in,
  input  R_W
);

  wire and_1_out, comparator_1_eq;

  Comparator #(.Bits(16)) comparator_1 (.a(MAR), .b(16'hfffe), .eq(comparator_1_eq));  // open: gt, lt
  and and_1 (and_1_out, comparator_1_eq, R_W, ~D_in[15]);  // And
  Stop stop_1 (.stop(and_1_out));
  // Pins of 1 and 16 bits meet at MAR
  // Pins of 1 and 16 bits meet at D_in
endmodule
