// Digital circuit lc3-halt_HDL.dig as structural Verilog
module lc3_halt_HDL (
  input  [15:0] MAR,
  input  start,
  input  R_W,
  input  Clock,
  input  reset,
  output Run
);

  wire and_1_out, and_2_out, and_3_out, and_4_out, m, or_1_out;

  Comparator #(.Bits(16)) comparator_1 (.a(MAR), .b(16'hfffe), .eq(m));  // open: gt, lt
  and and_1 (and_1_out, start, ~reset, ~m);  // And
  and and_2 (and_2_out, ~R_W, ~reset, Run);  // And
  and and_3 (and_3_out, start, ~reset, ~R_W);  // And
  and and_4 (and_4_out, ~m, ~reset, Run);  // And
  or or_1 (or_1_out, and_1_out, and_2_out, and_3_out, and_4_out);
  Register MCR (.D(or_1_out), .C(Clock), .en(Clock), .Q(Run));
endmodule
