// Digital circuit lc3-input-uart.dig as structural Verilog
module lc3_input_uart (
  input  [15:0] Addr,
  input  Clk,
  input  Serial,
  output [15:0] KBSR,
  output [15:0] KBDR
);

  wire comparator_1_eq, or_1_out;
  wire [7:0] u_uart_rx_rx_data;
  wire [15:15] KB_Status;

  Comparator #(.Bits(16)) comparator_1 (.a(16'hfe02), .b(Addr), .eq(comparator_1_eq));  // open: gt, lt
  uart_rx #(.applicationType("IVERILOG"), .iverilogOptions("-I \"C:\\Users\\allan\\source\\repos\\LC3_realized\\verilog\\experiments\\\" -p clk_freq=120000000 -p baud=115200 -p oversampling=8"), .CodeFile("C:\\Users\\allan\\source\\repos\\LC3_realized\\verilog\\experiments\\uart_rx.v")) u_uart_rx (
    .clk(Clk), .rx(Serial), .rx_ready(KB_Status[15]), .rx_data(u_uart_rx_rx_data));
  or or_1 (or_1_out, comparator_1_eq, KB_Status[15]);
  Register #(.Bits(16)) u_KBSR (.D({KB_Status[15], {15{1'b0}}}), .C(Clk), .en(or_1_out), .Q(KBSR));
  Register #(.Bits(16)) u_KBDR (.D({{8{1'b0}}, u_uart_rx_rx_data}), .C(Clk), .en(KB_Status[15]), .Q(KBDR));
endmodule
