// Digital circuit lc3-input_HDL.dig as structural Verilog
module lc3_input_HDL (
  input  [15:0] Addr,
  input  Clk,
  output [15:0] KBSR,
  output [15:0] KBDR
);

  wire comparator_1_eq, or_1_out;
  wire [7:0] u_lc3_input_data;
  wire [15:15] KB_Status;

  Comparator #(.Bits(16)) comparator_1 (.a(16'hfe02), .b(Addr), .eq(comparator_1_eq));  // open: gt, lt
  lc3_input #(.applicationType("IVERILOG"), .CodeFile("C:\\Users\\allan\\source\\repos\\LC3_realized\\lc3-input_HDL.v")) u_lc3_input (
    .clk(Clk), .data(u_lc3_input_data), .status(KB_Status[15]));
  or or_1 (or_1_out, comparator_1_eq, KB_Status[15]);
  Register #(.Bits(16)) u_KBSR (.D({KB_Status[15], {15{1'b0}}}), .C(Clk), .en(or_1_out), .Q(KBSR));
  Register #(.Bits(16)) u_KBDR (.D({{8{1'b0}}, u_lc3_input_data}), .C(Clk), .en(KB_Status[15]), .Q(KBDR));
endmodule
