// Digital circuit lc3-memmap.dig as structural Verilog
module lc3_memmap (
  input  [15:0] addr,
  input  en,
  input  R_W,
  output [1:0] MDR_Select,
  output MEM_EN,
  output LD_KBSR,
  output LD_DSR,
  output LD_DDR,
  output R_mapped
);

  wire comparator_1_eq, comparator_2_eq, comparator_3_eq, is_DDR, NotMapped;

  Comparator #(.Bits(16)) comparator_1 (.a(addr), .b(16'hfe00), .eq(comparator_1_eq));  // open: gt, lt
  Comparator #(.Bits(16)) comparator_2 (.a(addr), .b(16'hfe02), .eq(comparator_2_eq));  // open: gt, lt
  Comparator #(.Bits(16)) comparator_3 (.a(addr), .b(16'hfe04), .eq(comparator_3_eq));  // open: gt, lt
  Comparator #(.Bits(16)) comparator_4 (.a(addr), .b(16'hfe06), .eq(is_DDR));  // open: gt, lt
  nor nor_1 (NotMapped, comparator_1_eq, comparator_2_eq, comparator_3_eq);
  and and_1 (MEM_EN, en, NotMapped);
  PriorityEncoder #(.Selector_Bits(2)) priorityencoder_1 (
    .in0(comparator_1_eq), .in1(comparator_2_eq), .in2(comparator_3_eq), .in3(NotMapped), .num(MDR_Select));  // open: any
  and and_2 (LD_KBSR, comparator_1_eq, R_W);
  and and_3 (LD_DSR, comparator_3_eq, R_W);
  and and_4 (LD_DDR, is_DDR, R_W);
  or or_1 (R_mapped, ~NotMapped, is_DDR);  // Or
endmodule
