// Digital circuit lc3-memory.dig as structural Verilog
module lc3_memory (
  input  [15:0] Addr,
  input  [15:0] D_in,
  input  R_W,
  input  Clk,
  input  MIO_EN,
  input  [15:0] KBSR,
  input  [15:0] KBDR,
  input  [15:0] DSR,
  output [15:0] D_out,
  output R,
  output LD_KBSR,
  output LD_DSR,
  output LD_DDR
);

  wire and_1_out, and_2_out, counterpreset_1_ovf, MEM_EN, or_1_out, R_mapped;
  wire [1:0] lc3_memmap_1_mdr_select;
  wire [15:0] ramdualport_1_d;

  and and_1 (and_1_out, MEM_EN, R_W);
  and and_2 (and_2_out, MEM_EN, ~R_W);  // And
  lc3_memmap lc3_memmap_1 (
    .addr(Addr), .en(MIO_EN), .R_W(MEM_EN), .MDR_Select(lc3_memmap_1_mdr_select), .MEM_EN(MEM_EN),
    .LD_KBSR(LD_KBSR), .LD_DSR(LD_DSR), .LD_DDR(LD_DDR), .R_mapped(R_mapped));
  RAMDualPort #(.AddrBits(16), .isProgramMemory("true"), .Bits(16)) ramdualport_1 (
    .A(Addr), .Din(D_in), .str(and_1_out), .C(Clk), .ld(1'b1), .D(ramdualport_1_d));
  or or_1 (or_1_out, and_2_out, and_1_out);
  CounterPreset #(.maxValue(4), .Bits(3)) counterpreset_1 (
    .en(1'b1), .C(Clk), .dir(1'b0), .in(3'b000), .ld(1'b0), .clr(~or_1_out), .ovf(counterpreset_1_ovf));  // open: out
  Multiplexer #(.Selector_Bits(2), .Bits(16)) multiplexer_1 (
    .sel(lc3_memmap_1_mdr_select), .in_0(KBSR), .in_1(KBDR), .in_2(DSR), .in_3(ramdualport_1_d), .out(D_out));
  or or_2 (R, counterpreset_1_ovf, R_mapped);

  // Other names for the same wires on the sheet: R_W_t = MEM_EN
endmodule
