// Digital circuit lc3-microsequencer.dig as structural Verilog
module lc3_microsequencer (
  input  [5:0] J,
  input  [2:0] COND,
  input  IRD,
  input  INT,
  input  R,
  input  [4:0] IR_15_11,
  input  BEN,
  input  PSR_15,
  input  ACV,
  output [5:0] Addr
);

  wire and_1_out, and_2_out, and_3_out, and_4_out, and_5_out, and_6_out;
  wire [5:0] or_1_out;

  or or_1 (or_1_out[5], and_1_out, J[5]);
  and and_1 (and_1_out, ACV, ~COND[0], COND[1], COND[2]);  // And
  and and_2 (and_2_out, INT, COND[0], ~COND[1], COND[2]);  // And
  or or_2 (or_1_out[4], and_2_out, J[4]);
  or or_3 (or_1_out[3], and_3_out, J[3]);
  and and_3 (and_3_out, PSR_15, ~COND[0], ~COND[1], COND[2]);  // And
  and and_4 (and_4_out, BEN, ~COND[0], COND[1], ~COND[2]);  // And
  or or_4 (or_1_out[2], and_4_out, J[2]);
  or or_5 (or_1_out[1], and_5_out, J[1]);
  and and_5 (and_5_out, R, COND[0], ~COND[1], ~COND[2]);  // And
  Multiplexer #(.Bits(6)) multiplexer_1 (.sel(IRD), .in_0(or_1_out), .in_1({2'b00, IR_15_11[4:1]}), .out(Addr));
  and and_6 (and_6_out, IR_15_11[0], COND[0], COND[1], ~COND[2]);  // And
  or or_6 (or_1_out[0], and_6_out, J[0]);

  // Other names for the same wires on the sheet: IR_11 = IR_15_11[0]; IR_15_12[3:0] = IR_15_11[4:1]; J_0 = J[0];
  //   J_1 = J[1]; J_2 = J[2]; J_3 = J[3]; J_4 = J[4]; J_5 = J[5]
endmodule
