// Digital circuit lc3-output.dig as structural Verilog
module lc3_output (
  input  [15:0] D,
  input  Clk,
  input  en,
  output [15:0] DSR
);

  Register #(.Bits(16)) u_DSR (.D(16'h8000), .C(Clk), .en(Clk), .Q(DSR));
  Terminal terminal_1 (.D(D[7:0]), .C(Clk), .en(en));
endmodule
