// Digital circuit lc3-output_HDL.dig as structural Verilog
module lc3_output_HDL (
  input  [15:0] D,
  input  Clk,
  input  en,
  output [15:0] DSR,
  output [7:0] DDR
);

  wire [15:15] u_lc3_output_status;

  Register #(.Bits(16)) u_DSR (.D({u_lc3_output_status[15], {15{1'b0}}}), .C(Clk), .en(Clk), .Q(DSR));
  lc3_output #(.applicationType("IVERILOG"), .CodeFile("C:\\Users\\allan\\source\\repos\\LC3_realized\\lc3-output_HDL.v")) u_lc3_output (
    .clk(Clk), .data(D[7:0]), .enable(en), .status(u_lc3_output_status[15]));
  // Pins of 1 and 8 bits meet at D[7:0]

  assign DDR = D[7:0];
endmodule
