// Digital circuit lc3-pc-test.dig as structural Verilog
module lc3_pc_test (
  input  clk,
  input  [15:0] Addr,
  input  en,
  output [15:0] out_2
);

  pc #(.applicationType("IVERILOG"), .CodeFile("C:\\Users\\allan\\source\\repos\\LC3_realized\\lc3-pc.v")) u_pc (
    .addr_in(Addr), .clk(clk), .en(en), .addr_out(out_2));
endmodule
