// Digital circuit lc3-pc.dig as structural Verilog
module lc3_pc (
  input  [15:0] D,
  input  C,
  input  en,
  output [15:0] Q
);

  wire not_1_out, register_1_q, register_3_q;
  wire [15:0] register_2_q;

  Register register_1 (.D(1'b1), .C(C), .en(C), .Q(register_1_q));
  not not_1 (not_1_out, C);
  Register #(.Bits(16)) register_2 (.D(D), .C(C), .en(en), .Q(register_2_q));
  Register register_3 (.D(register_1_q), .C(C), .en(not_1_out), .Q(register_3_q));
  Multiplexer #(.Bits(16)) multiplexer_1 (.sel(register_3_q), .in_0(16'h3000), .in_1(register_2_q), .out(Q));
endmodule
