// Digital circuit lc3-register_file.dig as structural Verilog
module lc3_register_file (
  input  Clk,
  input  [15:0] Data,
  input  LD_Reg,
  input  [2:0] DR,
  input  [2:0] SR1,
  input  [2:0] SR2,
  output [15:0] SR2_OUT,
  output [15:0] SR1_OUT
);

  wire and_1_out, and_2_out, and_3_out, and_4_out, and_5_out, and_6_out, and_7_out, and_8_out, R0, R1, R2,
       R3, R4, R5, R6, R7;
  wire [15:0] R0_q, R1_q, R2_q, R3_q, R4_q, R5_q, R6_q, R7_q;

  Decoder #(.Selector_Bits(3)) decoder_1 (
    .sel(DR), .out_0(R0), .out_1(R1), .out_2(R2), .out_3(R3), .out_4(R4), .out_5(R5), .out_6(R6), .out_7(R7));
  and and_1 (and_1_out, LD_Reg, R0);
  and and_2 (and_2_out, LD_Reg, R1);
  and and_3 (and_3_out, LD_Reg, R2);
  and and_4 (and_4_out, LD_Reg, R3);
  and and_5 (and_5_out, LD_Reg, R4);
  and and_6 (and_6_out, LD_Reg, R5);
  and and_7 (and_7_out, LD_Reg, R6);
  and and_8 (and_8_out, LD_Reg, R7);
  Register #(.Bits(16)) u_R0 (.D(Data), .C(Clk), .en(and_1_out), .Q(R0_q));
  Register #(.Bits(16)) u_R1 (.D(Data), .C(Clk), .en(and_2_out), .Q(R1_q));
  Register #(.Bits(16)) u_R2 (.D(Data), .C(Clk), .en(and_3_out), .Q(R2_q));
  Register #(.Bits(16)) u_R3 (.D(Data), .C(Clk), .en(and_4_out), .Q(R3_q));
  Register #(.Bits(16)) u_R4 (.D(Data), .C(Clk), .en(and_5_out), .Q(R4_q));
  Register #(.Bits(16)) u_R5 (.D(Data), .C(Clk), .en(and_6_out), .Q(R5_q));
  Register #(.Bits(16), .isProgramCounter("true")) u_R6 (.D(Data), .C(Clk), .en(and_7_out), .Q(R6_q));
  Register #(.Bits(16)) u_R7 (.D(Data), .C(Clk), .en(and_8_out), .Q(R7_q));
  Multiplexer #(.Selector_Bits(3), .Bits(16)) multiplexer_1 (
    .sel(SR2), .in_0(R0_q), .in_1(R1_q), .in_2(R2_q), .in_3(R3_q), .in_4(R4_q), .in_5(R5_q), .in_6(R6_q),
    .in_7(R7_q), .out(SR2_OUT));
  Multiplexer #(.Selector_Bits(3), .Bits(16)) multiplexer_2 (
    .sel(SR1), .in_0(R0_q), .in_1(R1_q), .in_2(R2_q), .in_3(R3_q), .in_4(R4_q), .in_5(R5_q), .in_6(R6_q),
    .in_7(R7_q), .out(SR1_OUT));
endmodule
