// Digital circuit lc3.dig as structural Verilog
module lc3 (
  input  Clk
);

  wire ACV, ADDR1MUX, and_1_out, and_2_out, and_3_out, and_4_out, BEN, comparator_1_eq, comparator_2_eq,
       GateALU, GateMARMUX, GateMDR, GatePC, GatePSR, GateSP, GateVector, lc3_cc_logic_1_n, lc3_cc_logic_1_p,
       lc3_cc_logic_1_z, LD_ACV, LD_BEN, LD_CC, LD_DDR, LD_DSR, LD_IR, LD_KBSR, LD_MAR, LD_MDR, LD_PC,
       LD_Priv, LD_REG, LD_SavedSSP, LD_SavedUSP, LD_Vector, MARMUX, MEM_EN, MIO_EN, N, or_1_out, P, Priv,
       PSR_15, PSRMux, R, R_W, Set_Priv, SR2MUX, TableMux, Z;
  wire [1:0] ADDR2MUX, ALUK, DRMUX, MDR_Select, PCMUX, SPMUX, SR1MUX;
  wire [2:0] DR_nzp, driver_1_out, multiplexer_8_out, multiplexer_10_out, SR1;
  wire [4:0] Immed;
  wire [4:1] IR_15_11;
  wire [5:0] State;
  wire [6:0] driver_1_out_3;
  wire [7:0] multiplexer_11_out, Vector_q;
  wire [8:3] driver_1_out_2;
  wire [15:0] add_1_s, D_in, D_out, DSR, INMUX_out, KBDR, KBSR, keyboard_1_d, lc3_alu_1_alu, lc3_alu_2_alu,
       lc3_memory_1_p7, lc3_register_file_1_sr2_out, multiplexer_1_out, multiplexer_2_out, multiplexer_3_out,
       multiplexer_5_out, multiplexer_7_out, multiplexer_9_out, multiplexer_12_out, PC, plus_1_s,
       Saved_SSP_q, Saved_USP_q, SEXT_2_out, SEXT_3_out, SEXT_4_out, SEXT_out, SR1_OUT, sub_1_s;
  wire [15:15] KB_Data;

  Comparator #(.Bits(16)) comparator_1 (.a(PC), .b(16'h3006), .eq(comparator_1_eq));  // open: gt, lt
  Comparator #(.Bits(6)) comparator_2 (.a(State), .b(6'b010010), .eq(comparator_2_eq));  // open: gt, lt
  and and_1 (and_1_out, comparator_1_eq, comparator_2_eq);
  Register u_BEN (.D(or_1_out), .C(Clk), .en(LD_BEN), .Q(BEN));
  Break break_1 (.brk(and_1_out));
  or or_1 (or_1_out, and_4_out, and_3_out, and_2_out);
  // Probe on {IR_15_11, DR_nzp, SR1, SR2MUX, Immed}
  and and_2 (and_2_out, DR_nzp[2], N);
  and and_3 (and_3_out, DR_nzp[1], Z);
  and and_4 (and_4_out, DR_nzp[0], P);
  Register #(.Bits(16)) IR (
    .D({driver_1_out_3, driver_1_out_2, driver_1_out}), .C(Clk), .en(LD_IR),
    .Q({IR_15_11, DR_nzp, SR1, SR2MUX, Immed}));
  BitExtender #(.inputBits(6)) SEXT (.in({SR2MUX, Immed}), .out(SEXT_out));
  BitExtender #(.inputBits(9)) SEXT_2 (.in({SR1, SR2MUX, Immed}), .out(SEXT_2_out));
  BitExtender #(.inputBits(11)) SEXT_3 (.in({DR_nzp[1:0], SR1, SR2MUX, Immed}), .out(SEXT_3_out));
  lc3_acv lc3_acv_1 (.mode(PSR_15), .in(driver_1_out_3), .clk(Clk), .en(LD_ACV), .ACV(ACV));
  assign {driver_1_out_3, driver_1_out_2, driver_1_out} = GateMARMUX ? multiplexer_1_out : 16'bz;  // Driver driver_1
  Multiplexer #(.Bits(16)) multiplexer_1 (
    .sel(MARMUX), .in_0({{8{1'b0}}, SR1[1:0], SR2MUX, Immed}), .in_1(lc3_alu_1_alu), .out(multiplexer_1_out));
  Register u_Priv (.D(Priv), .C(Clk), .en(LD_Priv), .Q(PSR_15));
  Multiplexer #(.Selector_Bits(2), .Bits(16)) multiplexer_2 (
    .sel(ADDR2MUX), .in_0({16{1'b0}}), .in_1(SEXT_out), .in_2(SEXT_2_out), .in_3(SEXT_3_out),
    .out(multiplexer_2_out));
  Multiplexer #(.Bits(16)) multiplexer_3 (.sel(ADDR1MUX), .in_0(PC), .in_1(SR1_OUT), .out(multiplexer_3_out));
  LED u_N (.in(N));
  Register N_2 (.D(lc3_cc_logic_1_n), .C(Clk), .en(LD_CC), .Q(N));
  assign driver_1_out_3[6] = GatePSR ? PSR_15 : 1'bz;  // Driver driver_2
  Multiplexer multiplexer_4 (.sel(PSRMux), .in_0(Set_Priv), .in_1(driver_1_out_3[6]), .out(Priv));
  lc3_alu lc3_alu_1 (.ALU(lc3_alu_1_alu), .A(multiplexer_2_out), .B(multiplexer_3_out), .ALUK(2'b00));
  Register u_Z (.D(lc3_cc_logic_1_z), .C(Clk), .en(LD_CC), .Q(Z));
  lc3_cc_logic lc3_cc_logic_1 (
    .D_in({driver_1_out_3, driver_1_out_2, driver_1_out}), .N(lc3_cc_logic_1_n), .Z(lc3_cc_logic_1_z),
    .P(lc3_cc_logic_1_p));
  assign {driver_1_out_3, driver_1_out_2, driver_1_out} = GateMDR ? D_in : 16'bz;  // Driver driver_3
  LED Z_2 (.in(Z));
  Multiplexer #(.Bits(16)) multiplexer_5 (
    .sel(MIO_EN), .in_0({driver_1_out_3, driver_1_out_2, driver_1_out}), .in_1(INMUX_out),
    .out(multiplexer_5_out));
  Register #(.Bits(16)) MDR (.D(multiplexer_5_out), .C(Clk), .en(LD_MDR), .Q(D_in));
  // Probe on D_in
  LED u_P (.in(P));
  Register P_2 (.D(lc3_cc_logic_1_p), .C(Clk), .en(LD_CC), .Q(P));
  // lc3_control lc3_control_1: pin names not known; wires that end beside it: LD_MAR, Clk, LD_MDR, 1'b0, LD_IR, R, LD_BEN, {IR_15_11, DR_nzp[2]}, LD_REG, BEN, LD_CC, PSR_15, LD_PC, ACV, LD_Priv, LD_SavedSSP, LD_SavedUSP, LD_Vector, LD_ACV, GatePC, GateMDR, GateALU, GateMARMUX, GateVector, GatePSR, GateSP, PCMUX, DRMUX
  // lc3_memory lc3_memory_1: pin names not known; wires that end beside it: R, D_out, Clk, R_W, MEM_EN, D_in, lc3_memory_1_p7
  Multiplexer #(.Selector_Bits(2), .Bits(16)) multiplexer_6 (
    .sel(MDR_Select), .in_0(KBDR), .in_1(KBSR), .in_2(KBDR), .in_3(D_out), .out(INMUX_out));
  lc3_memmap lc3_memmap_1 (
    .addr(lc3_memory_1_p7), .en(MIO_EN), .R_W(R_W), .MDR_Select(MDR_Select), .MEM_EN(MEM_EN),
    .LD_KBSR(LD_KBSR), .LD_DSR(LD_DSR), .LD_DDR(LD_DDR));
  // Probe on PC
  Add #(.Bits(16)) plus_1 (.a(PC), .b(16'h1), .c_i(1'b0), .s(plus_1_s));  // open: c_o
  Multiplexer #(.Selector_Bits(2), .Bits(16)) multiplexer_7 (
    .sel(PCMUX), .in_0(plus_1_s), .in_1({driver_1_out_3, driver_1_out_2, driver_1_out}),
    .in_2(lc3_alu_1_alu), .in_3({16{1'b0}}), .out(multiplexer_7_out));
  Register #(.Bits(16)) MAR (
    .D({driver_1_out_3, driver_1_out_2, driver_1_out}), .C(Clk), .en(LD_MAR), .Q(lc3_memory_1_p7));
  // Probe on lc3_memory_1_p7
  assign {driver_1_out_3, driver_1_out_2, driver_1_out} = GatePC ? PC : 16'bz;  // Driver driver_4
  pc #(.applicationType("IVERILOG"), .CodeFile("\\home\\allan\\cs061\\LC3_realized\\lc3-pc.v")) u_pc (
    .addr_in(multiplexer_7_out), .clk(Clk), .en(LD_PC), .addr_out(PC));
  // Probe Bus on {driver_1_out_3, driver_1_out_2, driver_1_out}
  Keyboard keyboard_1 (.C(Clk), .en(1'b1), .D(keyboard_1_d), .av(KB_Data[15]));
  assign driver_1_out = GatePSR ? {N, Z, P} : 3'bz;  // Driver driver_5
  Register #(.Bits(16)) u_KBSR (.D({KB_Data[15], {15{1'b0}}}), .C(Clk), .en(LD_KBSR), .Q(KBSR));
  Register #(.Bits(16)) u_KBDR (.D(keyboard_1_d), .C(Clk), .en(KB_Data[15]), .Q(KBDR));
  Multiplexer #(.Selector_Bits(2), .Bits(3)) multiplexer_8 (
    .sel(DRMUX), .in_0(DR_nzp), .in_1(3'b111), .in_2(3'b110), .in_3(3'b000), .out(multiplexer_8_out));
  BitExtender #(.inputBits(5)) SEXT_4 (.in(Immed), .out(SEXT_4_out));
  // Probe State on State
  lc3_register_file lc3_register_file_1 (
    .Clk(Clk), .Data({driver_1_out_3, driver_1_out_2, driver_1_out}), .LD_Reg(LD_REG),
    .DR(multiplexer_8_out), .SR1(multiplexer_10_out), .SR2(Immed[2:0]),
    .SR2_OUT(lc3_register_file_1_sr2_out), .SR1_OUT(SR1_OUT));
  Multiplexer #(.Bits(16)) multiplexer_9 (
    .sel(SR2MUX), .in_0(lc3_register_file_1_sr2_out), .in_1(SEXT_4_out), .out(multiplexer_9_out));
  lc3_alu lc3_alu_2 (.ALU(lc3_alu_2_alu), .A(SR1_OUT), .B(multiplexer_9_out), .ALUK(ALUK));
  assign {driver_1_out_3, driver_1_out_2, driver_1_out} = GateALU ? lc3_alu_2_alu : 16'bz;  // Driver driver_6
  Multiplexer #(.Selector_Bits(2), .Bits(3)) multiplexer_10 (
    .sel(SR1MUX), .in_0(DR_nzp), .in_1(SR1), .in_2(3'b110), .in_3(3'b000), .out(multiplexer_10_out));
  Register #(.Bits(16)) u_DSR (.D(D_in), .C(Clk), .en(LD_DSR), .Q(DSR));
  Register #(.Bits(16)) DDR (.D(D_in), .C(Clk), .en(LD_DDR));  // open: Q
  Register #(.Bits(16)) Saved_SSP (.D(SR1_OUT), .C(Clk), .en(LD_SavedSSP), .Q(Saved_SSP_q));
  Register #(.Bits(16)) Saved_USP (.D(SR1_OUT), .C(Clk), .en(LD_SavedUSP), .Q(Saved_USP_q));
  Terminal terminal_1 (.D(keyboard_1_d), .C(Clk), .en(1'b1));
  Add #(.Bits(16)) add_1 (.a(SR1_OUT), .b(16'h1), .c_i(1'b0), .s(add_1_s));  // open: c_o
  Sub #(.Bits(16)) sub_1 (.a(SR1_OUT), .b(16'h1), .c_i(1'b0), .s(sub_1_s));  // open: c_o
  Multiplexer #(.Bits(8)) multiplexer_11 (
    .sel(TableMux), .in_0({driver_1_out_2[7:3], driver_1_out}), .in_1({8{1'b0}}), .out(multiplexer_11_out));
  Multiplexer #(.Selector_Bits(2), .Bits(16)) multiplexer_12 (
    .sel(SPMUX), .in_0(add_1_s), .in_1(sub_1_s), .in_2(Saved_SSP_q), .in_3(Saved_USP_q),
    .out(multiplexer_12_out));
  assign {driver_1_out_3, driver_1_out_2, driver_1_out} = GateVector ? {{8{1'b0}}, Vector_q} : 16'bz;  // Driver driver_7
  Register #(.Bits(8)) Vector (.D(multiplexer_11_out), .C(Clk), .en(LD_Vector), .Q(Vector_q));
  assign {driver_1_out_3, driver_1_out_2, driver_1_out} = GateSP ? multiplexer_12_out : 16'bz;  // Driver driver_8

  // Other names for the same wires on the sheet: SR2[2:0] = Immed[2:0]; IR_15_11[0] = DR_nzp[2]

  // Notes on the sheet:
  //   Input
  //   Output
endmodule
