// Digital circuit lc3_HDL.dig as structural Verilog
module lc3_HDL (
  input  RX,
  input  SPI__MOSI,
  input  Clock,
  output SPI__MISO,
  output SPI__SCK,
  output SPI__SS,
  output TX,
  output LED__B,
  output LED__G,
  output LED__R
);

  wire ACV, ADDR1MUX, BEN, GateALU, GateMARMUX, GateMDR, GatePC, GatePC_1, GatePSR, GateSP, GateVector,
       lc3_cc_logic_1_n, lc3_cc_logic_1_p, lc3_cc_logic_1_z, LD_ACV, LD_BEN, LD_CC, LD_DDR, LD_DSR, LD_IR,
       LD_KBSR, LD_MAR, LD_MDR, LD_PC, LD_Priv, LD_REG, LD_SavedSSP, LD_SavedUSP, LD_Vector, MARMUX, mem_op,
       MIO_EN, N, P, PSR_15, PSRMux, R, R_W, reset, running, rw, Set_Priv, SR2MUX, starting, TableMux,
       u_lc3_program_interface_led_b, Z;
  wire [1:0] ADDR2MUX, ALUK, DRMUX, PCMUX, SPMUX, SR1MUX;
  wire [2:0] IR_2_0, multiplexer_9_out, multiplexer_12_out, priorityencoder_1_num, SR1;
  wire [4:0] Immed;
  wire [4:1] IR_15_11;
  wire [5:0] State;
  wire [15:0] ADDER, addr, ALU, Bus, d__in, d__out, DSR, KBDR, KBSR, lc3_register_file_1_sr2_out, MAR, MAR_q,
       MARMUX_OUT, MDR_out, mem__in, multiplexer_2_out, multiplexer_3_out, multiplexer_4_out,
       multiplexer_6_out, multiplexer_11_out, PC, PC_1, plus_1_s, PSR, SEXT_2_out, SEXT_3_out, SEXT_4_out,
       SEXT_out, SP, SR1_OUT, Vector;

  Register #(.Bits(16)) IR (.D(Bus), .C(LED__G), .en(LD_IR), .Q({IR_15_11, IR_2_0, SR1, SR2MUX, Immed}));
  BitExtender #(.inputBits(6)) SEXT (.in({SR2MUX, Immed}), .out(SEXT_out));
  BitExtender #(.inputBits(9)) SEXT_2 (.in({SR1, SR2MUX, Immed}), .out(SEXT_2_out));
  BitExtender #(.inputBits(11)) SEXT_3 (.in({IR_2_0[1:0], SR1, SR2MUX, Immed}), .out(SEXT_3_out));
  lc3_halt_HDL lc3_halt_hdl_1 (.MAR(MAR), .start(starting), .R_W(R_W), .Clock(Clock), .reset(reset), .Run(running));
  Multiplexer #(.Bits(16)) multiplexer_1 (
    .sel(MARMUX), .in_0({{8{1'b0}}, SR1[1:0], SR2MUX, Immed}), .in_1(ADDER), .out(MARMUX_OUT));
  lc3_breakpoint lc3_breakpoint_1 (.Breakpoint({16{1'b0}}), .PC(PC), .State(State), .en(1'b0));
  Multiplexer #(.Selector_Bits(2), .Bits(16)) multiplexer_2 (
    .sel(ADDR2MUX), .in_0({16{1'b0}}), .in_1(SEXT_out), .in_2(SEXT_2_out), .in_3(SEXT_3_out),
    .out(multiplexer_2_out));
  Register register_1 (.D(lc3_cc_logic_1_n), .C(LED__G), .en(LD_CC), .Q(N));
  lc3_cc_logic lc3_cc_logic_1 (.D_in(Bus), .N(lc3_cc_logic_1_n), .Z(lc3_cc_logic_1_z), .P(lc3_cc_logic_1_p));
  and and_1 (LED__G, Clock, running);
  Multiplexer #(.Bits(16)) multiplexer_3 (.sel(ADDR1MUX), .in_0(PC), .in_1(SR1_OUT), .out(multiplexer_3_out));
  Register register_2 (.D(lc3_cc_logic_1_z), .C(LED__G), .en(LD_CC), .Q(Z));
  lc3_alu lc3_alu_1 (.ALU(ADDER), .A(multiplexer_2_out), .B(multiplexer_3_out), .ALUK(2'b00));
  Register register_3 (.D(lc3_cc_logic_1_p), .C(LED__G), .en(LD_CC), .Q(P));
  Register #(.Bits(16)) MDR (.D(multiplexer_4_out), .C(LED__G), .en(LD_MDR), .Q(MDR_out));
  lc3_program_interface #(.applicationType("IVERILOG"), .iverilogOptions("/home/allan/cs061/LC3_realized/uart_baud_tick_gen.v /home/allan/cs061/LC3_realized/uart_rx.v /home/allan/cs061/LC3_realized/uart_tx.v /home/allan/cs061/LC3_realized/spi_master.v"), .CodeFile("/home/allan/cs061/LC3_realized/lc3_program_interface.v")) u_lc3_program_interface (
    .Clock(Clock), .running_in(running), .RX(RX), .SPI_MOSI(SPI__MOSI), .mem_data_in(d__out),
    .SPI_MISO(SPI__MISO), .SPI_SCK(SPI__SCK), .SPI_SS(SPI__SS), .TX(TX),
    .LED_B(u_lc3_program_interface_led_b), .mem_addr_out(addr), .mem_data_out(d__in), .mem_rw_out(rw),
    .starting_out(starting), .reset_out(reset));  // open: LED_G, LED_R
  lc3_control lc3_control_1 (
    .Clk(LED__G), .INT(1'b0), .R(R), .IR_15_11({IR_15_11, IR_2_0[2]}), .BEN(BEN), .PSR_15(PSR_15), .ACV(ACV),
    .LD_MAR(LD_MAR), .LD_MDR(LD_MDR), .LD_IR(LD_IR), .LD_BEN(LD_BEN), .LD_REG(LD_REG), .LD_CC(LD_CC),
    .LD_PC(LD_PC), .LD_Priv(LD_Priv), .LD_SavedSSP(LD_SavedSSP), .LD_SavedUSP(LD_SavedUSP),
    .LD_Vector(LD_Vector), .LD_ACV(LD_ACV), .GatePC(GatePC), .GateMDR(GateMDR), .GateALU(GateALU),
    .GateMARMUX(GateMARMUX), .GateVector(GateVector), .GatePC_1(GatePC_1), .GatePSR(GatePSR),
    .GateSP(GateSP), .PCMUX(PCMUX), .DRMUX(DRMUX), .SR1MUX(SR1MUX), .ADDR2MUX(ADDR2MUX), .SPMUX(SPMUX),
    .ALUK(ALUK), .ADDR1MUX(ADDR1MUX), .MARMUX(MARMUX), .TableMUX(TableMux), .PSRMUX(PSRMux), .MIO_EN(MIO_EN),
    .R_W(R_W), .Set_Priv(Set_Priv), .State(State));
  Add #(.Bits(16)) _1 (.a(PC), .b({16{1'b1}}), .c_i(1'b0), .s(PC_1));  // open: c_o
  Multiplexer #(.Bits(16)) multiplexer_4 (.sel(MIO_EN), .in_0(Bus), .in_1(d__out), .out(multiplexer_4_out));
  Multiplexer multiplexer_5 (.sel(running), .in_0(rw), .in_1(R_W), .out(mem_op));
  Register register_4 (.D(1'b1), .C(Clock), .en(R), .Q(LED__R));
  Add #(.Bits(16)) plus_1 (.a(PC), .b(16'h1), .c_i(1'b0), .s(plus_1_s));  // open: c_o
  Multiplexer #(.Selector_Bits(2), .Bits(16)) multiplexer_6 (
    .sel(PCMUX), .in_0(plus_1_s), .in_1(Bus), .in_2(ADDER), .in_3({16{1'b0}}), .out(multiplexer_6_out));
  lc3_memory_HDL lc3_memory_hdl_1 (
    .Addr(MAR), .D_in(mem__in), .R_W(mem_op), .Clk(Clock), .MIO_EN(MIO_EN), .KBSR(KBSR), .KBDR(KBDR),
    .DSR(DSR), .running(running), .D_out(d__out), .R(R), .LD_KBSR(LD_KBSR), .LD_DSR(LD_DSR), .LD_DDR(LD_DDR));
  Multiplexer #(.Bits(16)) multiplexer_7 (.sel(running), .in_0(addr), .in_1(MAR_q), .out(MAR));
  pc #(.applicationType("IVERILOG"), .CodeFile("./lc3-pc.v")) u_pc (
    .D(multiplexer_6_out), .C(LED__G), .en(LD_PC), .Q(PC));
  Register #(.Bits(16)) u_MAR (.D(Bus), .C(LED__G), .en(LD_MAR), .Q(MAR_q));
  Multiplexer #(.Selector_Bits(3), .Bits(16)) multiplexer_8 (
    .sel(priorityencoder_1_num), .in_0(MARMUX_OUT), .in_1(PC_1), .in_2(PC), .in_3(ALU), .in_4(MDR_out),
    .in_5(PSR), .in_6(Vector), .in_7(SP), .out(Bus));
  PriorityEncoder #(.Selector_Bits(3)) priorityencoder_1 (
    .in0(GateMARMUX), .in1(GatePC_1), .in2(GatePC), .in3(GateALU), .in4(GateMDR), .in5(GatePSR),
    .in6(GateVector), .in7(GateSP), .num(priorityencoder_1_num));  // open: any
  Register #(.Bits(16)) u_KBSR (.D(16'h1), .C(LED__G), .en(LD_KBSR), .Q(KBSR));
  Register #(.Bits(16)) u_KBDR (.D(16'h1), .C(LED__G), .en(1'b1), .Q(KBDR));
  Multiplexer #(.Selector_Bits(2), .Bits(3)) multiplexer_9 (
    .sel(DRMUX), .in_0(IR_2_0), .in_1(3'b111), .in_2(3'b110), .in_3(3'b000), .out(multiplexer_9_out));
  Multiplexer #(.Bits(16)) multiplexer_10 (.sel(running), .in_0(d__in), .in_1(MDR_out), .out(mem__in));
  BitExtender #(.inputBits(5)) SEXT_4 (.in(Immed), .out(SEXT_4_out));
  lc3_register_file lc3_register_file_1 (
    .Clk(LED__G), .Data(Bus), .LD_Reg(LD_REG), .DR(multiplexer_9_out), .SR1(multiplexer_12_out),
    .SR2(Immed[2:0]), .SR2_OUT(lc3_register_file_1_sr2_out), .SR1_OUT(SR1_OUT));
  lc3_alu lc3_alu_2 (.ALU(ALU), .A(SR1_OUT), .B(multiplexer_11_out), .ALUK(ALUK));
  Multiplexer #(.Bits(16)) multiplexer_11 (
    .sel(SR2MUX), .in_0(lc3_register_file_1_sr2_out), .in_1(SEXT_4_out), .out(multiplexer_11_out));
  Multiplexer #(.Selector_Bits(2), .Bits(3)) multiplexer_12 (
    .sel(SR1MUX), .in_0(IR_2_0), .in_1(SR1), .in_2(3'b110), .in_3(3'b000), .out(multiplexer_12_out));
  Register #(.Bits(16)) u_DSR (.D(16'h1), .C(LED__G), .en(LD_DSR), .Q(DSR));
  Register #(.Bits(16)) DDR (.D(MDR_out), .C(LED__G), .en(LD_DDR));  // open: Q
  lc3_details_HDL lc3_details_hdl_1 (
    .Clk(LED__G), .LD_SavedSSP(LD_SavedSSP), .LD_SavedUSP(LD_SavedUSP), .SPMUX(SPMUX), .SR1_Val(SR1_OUT),
    .TableMux(TableMux), .LD_Vector(LD_Vector), .N(N), .Z(Z), .P(P), .IR_2_0(IR_2_0), .LD_BEN(LD_BEN),
    .LD_ACV(LD_ACV), .Set_Priv(Set_Priv), .PSRMux(PSRMux), .LD_Priv(LD_Priv), .Bus(Bus), .SP(SP),
    .Vector(Vector), .PSR(PSR), .BEN(BEN), .ACV(ACV), .PSR_15(PSR_15));

  assign LED__B = 1'b1;

  // Other names for the same wires on the sheet: SR2[2:0] = Immed[2:0]; IR_15_11[0] = IR_2_0[2]; Clk = LED__G

  // Notes on the sheet:
  //   Debug/Controls
  //   Input
  //   Output
endmodule
