// Digital circuit lc3_io.dig as structural Verilog
module lc3_io (
  input  in_5,
  input  in_6,
  input  [15:0] in_7,
  input  in_8,
  input  [15:0] in_9,
  input  in_10,
  output out_1,
  output [15:0] KBDR,
  output tx__start,
  output [15:0] DDR
);

  wire [14:0] u_lc3_input_kbsr_out, u_lc3_output_dsr_out;

  lc3_input #(.applicationType("IVERILOG"), .CodeFile("/home/allan/cs061/lc3-io/lc3_input.v")) u_lc3_input (
    .data_ready(in_5), .read(in_6), .data_in(in_7), .kbsr_out({out_1, u_lc3_input_kbsr_out}), .kbdr_out(KBDR));
  lc3_output #(.applicationType("IVERILOG"), .CodeFile("/home/allan/cs061/lc3-io/lc3_output.v")) u_lc3_output (
    .ld_ddr(in_8), .ddr_in(in_9), .tx_busy(in_10), .dsr_out({tx__start, u_lc3_output_dsr_out}), .ddr_out(DDR));
endmodule
